# Fritzing sketch MIDI Stepper V1 (saved by Fritzing 0.9.3b)
breadboards: 1

parts:
  Part1 = Arduino Uno (Rev3)
  Pololu_A1 = Pololu A4988 [package=SO16]
  R1 = Resistor [tolerance=±5% resistance=10k package=THT]
  C1 = Electrolytic Capacitor [capacitance=100µF package="100 mil [THT, electrolytic]"]
  M1 = Stepper Motor - Bipolar
  Pololu_A2 = Pololu A4988 [package=SO16]
  C2 = Electrolytic Capacitor [capacitance=100µF package="100 mil [THT, electrolytic]"]
  M2 = Stepper Motor - Bipolar
  Pololu_A3 = Pololu A4988 [package=SO16]
  C3 = Electrolytic Capacitor [capacitance=100µF package="100 mil [THT, electrolytic]"]
  M3 = Stepper Motor - Bipolar
  Pololu_A4 = Pololu A4988 [package=SO16]
  C4 = Electrolytic Capacitor [capacitance=100µF package="100 mil [THT, electrolytic]"]
  M4 = Stepper Motor - Bipolar
  Power_plug1 = Power plug

nets (from the breadboard view):
  N1: Part1.D8, Pololu_A1.ENABLE, R1.Pin_0, Pololu_A2.ENABLE, Pololu_A3.ENABLE, Pololu_A4.ENABLE
  N2: Part1.D12/MISO, Pololu_A2.STEP
  GND: Part1.GND, Pololu_A1.DIR, Pololu_A1.GND, C1.-, Pololu_A2.DIR, Pololu_A2.GND, C2.-, Pololu_A3.DIR, Pololu_A3.GND, C3.-, Pololu_A4.DIR, Pololu_A4.GND, C4.-, Power_plug1.GND
  N3: Part1.D2, Pololu_A4.STEP
  N4: Part1.D3_PWM, Pololu_A3.STEP
  N5: Part1.D4, Pololu_A1.STEP
  VDD: Part1.5V, Pololu_A1.VDD, R1.Pin_1, Pololu_A2.VDD, Pololu_A3.VDD, Pololu_A4.VDD
  N6: Pololu_A1.RESET, Pololu_A1.SLEEP
  N7: Pololu_A1.1B, M1.D
  N8: Pololu_A1.1A, M1.B
  N9: Pololu_A1.2A, M1.C
  N10: Pololu_A1.2B, M1.A
  N11: Pololu_A1.VMOT, C1.+, Pololu_A2.VMOT, C2.+, Pololu_A3.VMOT, C3.+, Pololu_A4.VMOT, C4.+, Power_plug1.VCC
  N12: Pololu_A2.RESET, Pololu_A2.SLEEP
  N13: Pololu_A2.1B, M2.D
  N14: Pololu_A2.1A, M2.B
  N15: Pololu_A2.2A, M2.C
  N16: Pololu_A2.2B, M2.A
  N17: Pololu_A3.RESET, Pololu_A3.SLEEP
  N18: Pololu_A3.1B, M3.D
  N19: Pololu_A3.1A, M3.B
  N20: Pololu_A3.2A, M3.C
  N21: Pololu_A3.2B, M3.A
  N22: Pololu_A4.RESET, Pololu_A4.SLEEP
  N23: Pololu_A4.1B, M4.D
  N24: Pololu_A4.1A, M4.B
  N25: Pololu_A4.2A, M4.C
  N26: Pololu_A4.2B, M4.A

notes:
  Enable Pullup
  MIDI Stepper Schematic
